# Fritzing sketch Sketch (saved by Fritzing 0.9.3b)
breadboards: 1

parts:
  Componente1 = Arduino Uno (Rev3) - ICSP
  HC-SR04_Sensor_1 = HC-SR04 Ultrasonic Distance Sensor
  LED1 = smd LED [color="Red (633nm)" package="0805 [SMD]"]

nets:
  5V: Componente1.5V, HC-SR04_Sensor_1.VCC
  GND: Componente1.GND, HC-SR04_Sensor_1.GND, LED1.anode
  N1: Componente1.D13/SCK, LED1.cathode
  N2: Componente1.D2, HC-SR04_Sensor_1.TRIG
  N3: Componente1.D3_PWM, HC-SR04_Sensor_1.ECHO

// code stored in the sketch: sensor_proximidad.ino
const int Trigger = 2;   //Pin digital 2 para el Trigger del sensor
const int Echo = 3;   //Pin digital 3 para el Echo del sensor

void setup() {
  Serial.begin(9600);//iniciailzamos la comunicación
  pinMode(Trigger, OUTPUT); //pin como salida
  pinMode(Echo, INPUT);  //pin como entrada
  pinMode(13, OUTPUT); 
  digitalWrite(Trigger, LOW);//Inicializamos el pin con 0
  digitalWrite(13, LOW);
}

void loop()
{

  long t; //timepo que demora en llegar el eco
  long d; //distancia en centimetros
  
  digitalWrite(Trigger, HIGH);
  delayMicroseconds(10);          //Enviamos un pulso de 10us
  digitalWrite(Trigger, LOW);
  
  t = pulseIn(Echo, HIGH); //obtenemos el ancho del pulso
  d = t/59;             //escalamos el tiempo a una distancia en cm
  
  Serial.print("Distancia: ");
  Serial.print(d);      //Enviamos serialmente el valor de la distancia
  if(d<=9){
    digitalWrite(13, HIGH);
  }else{
    digitalWrite(13, LOW);
  }
  Serial.print("cm");
  Serial.println();
  delay(100);          //Hacemos una pausa de 100ms
}
